// Logisim project A2 group 4 8bit pc.circ as structural Verilog: 9 circuits, main circuit main
module main (
  input  reset,
  output [7:0] out_2,
  output [7:0] out_3,
  output [7:0] out_4,
  output [7:0] out_5,
  output [7:0] out_6
);

  wire alu_1_out_4, and_1_out, and_2_out, clock_1_out, isstack_1_out_2, not_1_out, or_1_out;
  wire [3:0] instruction_memory_1_instruction_2, multiplexer_1_out;
  wire [7:0] adder_1_out, adder_2_out, data_stack_memory_1_out_8, multiplexer_3_out, p_c_1_out_4,
       register_s_1_out_9, shifter_1_out_4;
  wire [13:0] control_1_out_2;
  wire [15:0] instruction_memory_1_instruction;

  P_C p_c_1 (.in_1(out_2), .out_4(p_c_1_out_4), .in_2(clock_1_out), .in_3(reset));
  Clock clock_1 (.out(clock_1_out));
  Adder adder_1 (.a(p_c_1_out_4), .b(8'h1), .out(adder_1_out));  // open: cin, cout
  Control control_1 (.in_1(instruction_memory_1_instruction_2), .out_2(control_1_out_2));
  Instruction_Memory instruction_memory_1 (
    .Address(p_c_1_out_4),
    .Instruction({instruction_memory_1_instruction_2, instruction_memory_1_instruction}));
  Multiplexer #(.width(4), .enable("false")) multiplexer_1 (
    .in0(instruction_memory_1_instruction[11:8]), .in1(instruction_memory_1_instruction[7:4]),
    .out(multiplexer_1_out), .sel(control_1_out_2[10]));
  Register_s register_s_1 (
    .Write_reg(multiplexer_1_out), .in_4(out_6), .out_8(out_3), .out_9(register_s_1_out_9),
    .in_1(control_1_out_2[13]), .Read_reg1(instruction_memory_1_instruction[15:12]), .Clock(clock_1_out),
    .reset(reset), .Readreg2(instruction_memory_1_instruction[11:8]));
  Multiplexer #(.width(8), .enable("false")) multiplexer_2 (
    .in0(register_s_1_out_9), .in1(instruction_memory_1_instruction[7:0]), .out(out_5),
    .sel(control_1_out_2[9]));
  ALU alu_1 (.in_2(out_3), .in_3(out_5), .out_4(alu_1_out_4), .out_5(out_4), .in_1(control_1_out_2[5:3]));
  isStack isstack_1 (.in_1(instruction_memory_1_instruction[15:12]), .out_2(isstack_1_out_2));
  Adder adder_2 (.a(adder_1_out), .b(instruction_memory_1_instruction[7:0]), .out(adder_2_out));  // open: cin, cout
  and and_1 (and_1_out, control_1_out_2[7], alu_1_out_4);
  not not_1 (not_1_out, alu_1_out_4);
  Multiplexer #(.width(8), .enable("false")) multiplexer_3 (
    .in0(adder_1_out), .in1(adder_2_out), .out(multiplexer_3_out), .sel(or_1_out));
  and and_2 (and_2_out, control_1_out_2[6], not_1_out);
  Shifter shifter_1 (
    .in_2(out_4), .in_3(instruction_memory_1_instruction[3:0]), .out_4(shifter_1_out_4),
    .in_1(control_1_out_2[1:0]));
  or or_1 (or_1_out, and_1_out, and_2_out);
  Multiplexer #(.width(8), .enable("false")) multiplexer_4 (
    .in0(multiplexer_3_out), .in1(instruction_memory_1_instruction[15:8]), .out(out_2),
    .sel(control_1_out_2[2]));
  Data___Stack_Memory data_stack_memory_1 (
    .in_2(shifter_1_out_4), .in_3(register_s_1_out_9), .out_8(data_stack_memory_1_out_8),
    .MemWrite(control_1_out_2[11]), .Clock(clock_1_out), .MemRead(control_1_out_2[12]),
    .isStack(isstack_1_out_2), .reset(reset));
  Multiplexer #(.width(8), .enable("false")) multiplexer_5 (
    .in0(shifter_1_out_4), .in1(data_stack_memory_1_out_8), .out(out_6), .sel(control_1_out_2[8]));
endmodule

module Instruction_Memory (
  input  [7:0] Address,
  output [19:0] Instruction
);

  ROM #(.dataWidth(20)) rom_1 (.addr(Address), .data(Instruction));  // open: sel

  // Notes on the sheet:
  //   contents of rom_1 (hex, n*v repeats v):
  //   a5609 c2650 36320 512f5 e4630 45001 20e00 70331 55307 d5507 f55fb d15f5 56fd 20500
endmodule

module Control (
  input  [3:0] in_1,
  output [13:0] out_2
);

  ROM #(.addrWidth(4), .dataWidth(14)) rom_1 (.addr(in_1), .data(out_2));  // open: sel

  // Notes on the sheet:
  //   contents of rom_1 (hex, n*v repeats v):
  //   88 2210 4 2420 48 a00 2400 2401 2410 2402 2200 2218 2418 3300 2408 2208
endmodule

module ALU (
  input  [2:0] in_1,
  input  [7:0] in_2,
  input  [7:0] in_3,
  output out_4,
  output [7:0] out_5
);

  wire [7:0] adder_1_out, and_1_out, nor_1_out, or_1_out, subtractor_1_out;

  Adder adder_1 (.a(in_2), .b(in_3), .out(adder_1_out));  // open: cin, cout
  Subtractor subtractor_1 (.a(in_2), .b(in_3), .out(subtractor_1_out));  // open: bin, bout
  assign and_1_out = in_2 & in_3;  // AND_Gate and_1, 8 bits wide
  assign or_1_out = in_2 | in_3;  // OR_Gate or_1, 8 bits wide
  assign nor_1_out = ~(in_2 | in_3);  // NOR_Gate nor_1, 8 bits wide
  Multiplexer #(.select(3), .width(8), .enable("false")) multiplexer_1 (
    .in0(adder_1_out), .in1(subtractor_1_out), .in2(and_1_out), .in3(or_1_out), .in4(nor_1_out), .out(out_5),
    .sel(in_1));  // open: in5, in6, in7
  Comparator comparator_1 (.a(out_5), .b({8{1'b0}}), .eq(out_4));  // open: gt, lt
endmodule

module Shifter (
  input  [1:0] in_1,
  input  [7:0] in_2,
  input  [3:0] in_3,
  output [7:0] out_4
);

  wire [15:0] bit_extender_1_out, shifter_1_out, shifter_2_out;
  wire [15:8] multiplexer_1_out;

  assign bit_extender_1_out = {{8{1'b0}}, in_2};  // Bit_Extender bit_extender_1
  Shifter_part #(.width(16), .shift("lr")) shifter_1 (.in(bit_extender_1_out), .\dist (in_3), .out(shifter_1_out));
  Shifter_part #(.width(16)) shifter_2 (.in(bit_extender_1_out), .\dist (in_3), .out(shifter_2_out));
  Multiplexer #(.select(2), .width(16)) multiplexer_1 (
    .in0(bit_extender_1_out), .in1(shifter_1_out), .in2(shifter_2_out), .out({multiplexer_1_out, out_4}),
    .sel(in_1));  // open: in3, en
endmodule

module isStack (
  input  [3:0] in_1,
  output out_2
);

  Comparator #(.width(4)) comparator_1 (.a(in_1), .b(4'b0001), .eq(out_2));  // open: gt, lt
endmodule

module Register_s (
  input  in_1,
  input  [3:0] Read_reg1,
  input  [3:0] Write_reg,
  input  [7:0] in_4,
  input  [3:0] Readreg2,
  input  Clock,
  input  reset,
  output [7:0] out_8,
  output [7:0] out_9
);

  wire and_1_out, and_2_out, and_3_out, and_4_out, and_5_out, and_6_out, and_7_out, decoder_1_out0,
       decoder_1_out1, decoder_1_out2, decoder_1_out3, decoder_1_out4, decoder_1_out5, decoder_1_out6;
  wire [7:0] register_1_q, register_2_q, register_3_q, register_4_q, register_5_q, register_6_q, register_7_q;

  Decoder #(.select(4), .enable("false")) decoder_1 (
    .out0(decoder_1_out0), .out1(decoder_1_out1), .out2(decoder_1_out2), .out3(decoder_1_out3),
    .out4(decoder_1_out4), .out5(decoder_1_out5), .out6(decoder_1_out6), .sel(Write_reg));  // open: out7, out8, out9, out10, out11, out12, out13, out14, out15
  Register register_1 (.D(in_4), .en(and_1_out), .Q(register_1_q), .clk(Clock), .clr(reset));
  and and_1 (and_1_out, decoder_1_out0, in_1);
  Register register_2 (.D(in_4), .en(and_2_out), .Q(register_2_q), .clk(Clock), .clr(reset));
  and and_2 (and_2_out, decoder_1_out1, in_1);
  Register register_3 (.D(in_4), .en(and_3_out), .Q(register_3_q), .clk(Clock), .clr(reset));
  and and_3 (and_3_out, decoder_1_out2, in_1);
  Register register_4 (.D(in_4), .en(and_4_out), .Q(register_4_q), .clk(Clock), .clr(reset));
  and and_4 (and_4_out, decoder_1_out3, in_1);
  Register register_5 (.D(in_4), .en(and_5_out), .Q(register_5_q), .clk(Clock), .clr(reset));
  and and_5 (and_5_out, decoder_1_out4, in_1);
  Register register_6 (.D(in_4), .en(and_6_out), .Q(register_6_q), .clk(Clock), .clr(reset));
  and and_6 (and_6_out, decoder_1_out5, in_1);
  Register register_7 (.D(in_4), .en(and_7_out), .Q(register_7_q), .clk(Clock), .clr(reset));
  and and_7 (and_7_out, decoder_1_out6, in_1);
  Multiplexer #(.select(4), .width(8), .enable("false")) multiplexer_1 (
    .in0(register_1_q), .in1(register_2_q), .in2(register_3_q), .in3(register_4_q), .in4(register_5_q),
    .in5(register_6_q), .in6(register_7_q), .out(out_8), .sel(Read_reg1));  // open: in7, in8, in9, in10, in11, in12, in13, in14, in15
  Multiplexer #(.select(4), .width(8), .enable("false")) multiplexer_2 (
    .in0(register_1_q), .in1(register_2_q), .in2(register_3_q), .in3(register_4_q), .in4(register_5_q),
    .in5(register_6_q), .in6(register_7_q), .out(out_9), .sel(Readreg2));  // open: in7, in8, in9, in10, in11, in12, in13, in14, in15
endmodule

module Data___Stack_Memory (
  input  MemWrite,
  input  [7:0] in_2,
  input  [7:0] in_3,
  input  MemRead,
  input  isStack,
  input  Clock,
  input  reset,
  output [7:0] out_8
);

  wire and_1_out, and_2_out, and_3_out, and_4_out, not_1_out, not_2_out;
  wire [7:0] ram_1_data, ram_2_data;

  and and_1 (and_1_out, MemWrite, isStack);
  and and_2 (and_2_out, MemWrite, not_1_out);
  not not_1 (not_1_out, isStack);
  and and_3 (and_3_out, MemRead, not_2_out);
  RAM #(.bus("separate")) ram_1 (
    .addr(in_2), .din(in_3), .data(ram_1_data), .str(and_1_out), .clk(Clock), .ld(and_4_out), .clr(reset));  // open: sel
  and and_4 (and_4_out, MemRead, isStack);
  RAM #(.bus("separate")) ram_2 (
    .addr(in_2), .din(in_3), .data(ram_2_data), .str(and_2_out), .clk(Clock), .ld(and_3_out), .clr(reset));  // open: sel
  not not_2 (not_2_out, isStack);
  Multiplexer #(.width(8), .enable("false")) multiplexer_1 (
    .in0(ram_2_data), .in1(ram_1_data), .out(out_8), .sel(isStack));

  // Notes on the sheet:
  //   Stack Memory
  //   Data Memory
endmodule

module P_C (
  input  [7:0] in_1,
  input  in_2,
  input  in_3,
  output [7:0] out_4
);

  Register register_1 (.D(in_1), .Q(out_4), .clk(in_2), .clr(in_3));  // open: en
endmodule
