// Logisim project A2 group 4 8bit pc.circ as structural Verilog: 9 circuits, main circuit main
module main (
  input  reset,
  output [7:0] out_2,
  output [7:0] out_3,
  output [7:0] out_4,
  output [7:0] out_5,
  output [7:0] out_6
);

  wire alu_1_zero, and_1_out, and_2_out, clock_out, isstack_1_is_stack_memory, not_1_out, or_1_out;
  wire [3:0] instruction_memory_1__20_bit_instruction_2, multiplexer_1_out;
  wire [7:0] adder_1_out, adder_2_out, data_stack_memory_1_readdata, multiplexer_3_out, pc_1_current_address,
       register_s_1_read_data_2, shifter_1_sfited_data_8___bit;
  wire [13:0] control_1__14___bit_selector;
  wire [15:0] instruction_memory_1__20_bit_instruction;

  PC pc_1 (.Next_Address(out_2), .Current_Address(pc_1_current_address), .clock(clock_out), .reset(reset));
  Clock clock (.out(clock_out));
  Adder adder_1 (.a(pc_1_current_address), .b(8'h1), .out(adder_1_out));  // open: cin, cout
  Instruction_Memory instruction_memory_1 (
    ._8_bit_Address_of_current_instruction(pc_1_current_address),
    ._20_bit_Instruction({instruction_memory_1__20_bit_instruction_2, instruction_memory_1__20_bit_instruction}));
  Control control_1 (
    .Opcode(instruction_memory_1__20_bit_instruction_2), ._14___bit_selector(control_1__14___bit_selector));
  Multiplexer #(.width(4), .enable("false")) multiplexer_1 (
    .in0(instruction_memory_1__20_bit_instruction[11:8]),
    .in1(instruction_memory_1__20_bit_instruction[7:4]), .out(multiplexer_1_out),
    .sel(control_1__14___bit_selector[10]));
  Register_s register_s_1 (
    .Write_reg_4_bit(multiplexer_1_out), .write_data_8_bit(out_6), .read_data_1(out_3),
    .read_data_2(register_s_1_read_data_2), .RegWrite(control_1__14___bit_selector[13]),
    .Read_reg1(instruction_memory_1__20_bit_instruction[15:12]), .Clock(clock_out), .reset(reset),
    .Read_reg2(instruction_memory_1__20_bit_instruction[11:8]));
  DotMatrix #(.inputtype("row"), .matrixcols(8), .matrixrows(1)) dotmatrix_1 (.row0(out_3));
  Multiplexer #(.width(8), .enable("false")) multiplexer_2 (
    .in0(register_s_1_read_data_2), .in1(instruction_memory_1__20_bit_instruction[7:0]), .out(out_5),
    .sel(control_1__14___bit_selector[9]));
  ALU alu_1 (
    ._8___bit_data_input_1(out_3), ._8___bit_data_input_2(out_5), .Zero(alu_1_zero), .ALU_result(out_4),
    .ALU_operation_0_to_4(control_1__14___bit_selector[5:3]));
  DotMatrix #(.inputtype("row"), .matrixcols(8), .matrixrows(1)) dotmatrix_2 (.row0(out_5));
  Adder adder_2 (
    .a(adder_1_out), .b(instruction_memory_1__20_bit_instruction[7:0]), .out(adder_2_out));  // open: cin, cout
  not not_1 (not_1_out, alu_1_zero);
  DotMatrix #(.inputtype("row"), .matrixcols(8), .matrixrows(1)) dotmatrix_3 (.row0(out_4));
  isStack isstack_1 (
    .Register_Address_R_W(instruction_memory_1__20_bit_instruction[15:12]),
    .is_stack_memory(isstack_1_is_stack_memory));
  and and_1 (and_1_out, control_1__14___bit_selector[7], alu_1_zero);
  and and_2 (and_2_out, control_1__14___bit_selector[6], not_1_out);
  Shifter shifter_1 (
    ._8_bit_input(out_4), .shamt_4_bit(instruction_memory_1__20_bit_instruction[3:0]),
    .sfited_data_8___bit(shifter_1_sfited_data_8___bit),
    ._0_no_shift__1_right_shift__2_left_shift(control_1__14___bit_selector[1:0]));
  Multiplexer #(.width(8), .enable("false")) multiplexer_3 (
    .in0(adder_1_out), .in1(adder_2_out), .out(multiplexer_3_out), .sel(or_1_out));
  or or_1 (or_1_out, and_1_out, and_2_out);
  Multiplexer #(.width(8), .enable("false")) multiplexer_4 (
    .in0(multiplexer_3_out), .in1(instruction_memory_1__20_bit_instruction[15:8]), .out(out_2),
    .sel(control_1__14___bit_selector[2]));
  Data___Stack_Memory data_stack_memory_1 (
    .Address(shifter_1_sfited_data_8___bit), .WriteData(register_s_1_read_data_2),
    .ReadData(data_stack_memory_1_readdata), .MemWrite(control_1__14___bit_selector[11]), .Clock(clock_out),
    .MemRead(control_1__14___bit_selector[12]), .isStack(isstack_1_is_stack_memory), .reset(reset));
  DotMatrix #(.inputtype("row"), .matrixcols(8), .matrixrows(1)) dotmatrix_4 (.row0(out_2));
  DotMatrix #(.inputtype("row"), .matrixcols(8), .matrixrows(1)) dotmatrix_5 (.row0(out_6));
  Multiplexer #(.width(8), .enable("false")) multiplexer_5 (
    .in0(shifter_1_sfited_data_8___bit), .in1(data_stack_memory_1_readdata), .out(out_6),
    .sel(control_1__14___bit_selector[8]));

  // Notes on the sheet:
  //   PC + 1
  //   Opcode
  //   Addr / Imm
  //   RegDst
  //   RegWrite
  //   sr1
  //   rd1
  //   r2
  //   w
  //   rd2
  //   WriteData
  //   ALUSrc
  //   ALUOp
  //   Zero
  //   ALUResult
  //   Breq
  //   Brne
  //   branch target
  //   ShiftChoice
  //   shamt
  //   Jump adress
  //   PCSrc
  //   Jump
  //   MemWrite
  //   Address
  //   WriteData
  //   isStack
  //   MemtoReg
  //   MemRead
  //   ReadData
  //   FULL DATAPATH
endmodule

module Instruction_Memory (
  input  [7:0] _8_bit_Address_of_current_instruction,
  output [19:0] _20_bit_Instruction
);

  ROM #(.dataWidth(20)) rom_1 (.addr(_8_bit_Address_of_current_instruction), .data(_20_bit_Instruction));  // open: sel

  // Notes on the sheet:
  //   INSTRUCTION MEMORY
  //   Instruction Memory(ROM) loaded from logisim.txt
  //   8-bit address, 20-bit data
  //   contents of rom_1 (hex, n*v repeats v):
  //   a5609 c2650 36320 512f5 e4630 45001 20e00 70331 55307 d5507 f55fb d15f5 56fd 20500
endmodule

module Control (
  input  [3:0] Opcode,
  output [13:0] _14___bit_selector
);

  ROM #(.addrWidth(4), .dataWidth(14)) rom_1 (.addr(Opcode), .data(_14___bit_selector));  // open: sel

  // Notes on the sheet:
  //   CONTROL
  //   contents of rom_1 (hex, n*v repeats v):
  //   88 2210 4 2420 48 a00 2400 2401 2410 2402 2200 2218 2418 3300 2408 2208
endmodule

module ALU (
  input  [2:0] ALU_operation_0_to_4,
  input  [7:0] _8___bit_data_input_1,
  input  [7:0] _8___bit_data_input_2,
  output Zero,
  output [7:0] ALU_result
);

  wire [7:0] adder_1_out, and_1_out, nor_1_out, or_1_out, subtractor_1_out;

  Adder adder_1 (.a(_8___bit_data_input_1), .b(_8___bit_data_input_2), .out(adder_1_out));  // open: cin, cout
  Subtractor subtractor_1 (
    .a(_8___bit_data_input_1), .b(_8___bit_data_input_2), .out(subtractor_1_out));  // open: bin, bout
  assign and_1_out = _8___bit_data_input_1 & _8___bit_data_input_2;  // AND_Gate and_1, 8 bits wide
  assign or_1_out = _8___bit_data_input_1 | _8___bit_data_input_2;  // OR_Gate or_1, 8 bits wide
  assign nor_1_out = ~(_8___bit_data_input_1 | _8___bit_data_input_2);  // NOR_Gate nor_1, 8 bits wide
  Multiplexer #(.select(3), .width(8), .enable("false")) multiplexer_1 (
    .in0(adder_1_out), .in1(subtractor_1_out), .in2(and_1_out), .in3(or_1_out), .in4(nor_1_out),
    .out(ALU_result), .sel(ALU_operation_0_to_4));  // open: in5, in6, in7
  Comparator comparator_1 (.a(ALU_result), .b({8{1'b0}}), .eq(Zero));  // open: gt, lt

  // Notes on the sheet:
  //   ALU 8-bit
  //   add
  //   sub
  //   and
  //   or
  //   nor
endmodule

module Shifter (
  input  [1:0] _0_no_shift__1_right_shift__2_left_shift,
  input  [7:0] _8_bit_input,
  input  [3:0] shamt_4_bit,
  output [7:0] sfited_data_8___bit
);

  wire [15:0] bit_extender_1_out, shifter_1_out, shifter_2_out;
  wire [15:8] multiplexer_1_out;

  assign bit_extender_1_out = {{8{1'b0}}, _8_bit_input};  // Bit_Extender bit_extender_1
  Shifter_part #(.width(16), .shift("lr")) shifter_1 (
    .in(bit_extender_1_out), .\dist (shamt_4_bit), .out(shifter_1_out));
  Shifter_part #(.width(16)) shifter_2 (.in(bit_extender_1_out), .\dist (shamt_4_bit), .out(shifter_2_out));
  Multiplexer #(.select(2), .width(16)) multiplexer_1 (
    .in0(bit_extender_1_out), .in1(shifter_1_out), .in2(shifter_2_out),
    .out({multiplexer_1_out, sfited_data_8___bit}), .sel(_0_no_shift__1_right_shift__2_left_shift));  // open: in3, en

  // Notes on the sheet:
  //   unsigned bit extender
  //   SHIFTER
  //   no shift
  //   right shift
  //   left shift
  //   shifted data
endmodule

module isStack (
  input  [3:0] Register_Address_R_W,
  output is_stack_memory
);

  Comparator #(.width(4)) comparator_1 (.a(Register_Address_R_W), .b(4'b0001), .eq(is_stack_memory));  // open: gt, lt

  // Notes on the sheet:
  //   isSTACK
  //   check if register value is 1 as we defined $sp at address 0001
endmodule

module Register_s (
  input  RegWrite,
  input  [3:0] Read_reg1,
  input  [3:0] Write_reg_4_bit,
  input  [7:0] write_data_8_bit,
  input  [3:0] Read_reg2,
  input  Clock,
  input  reset,
  output [7:0] read_data_1,
  output [7:0] read_data_2
);

  wire and_1_out, and_2_out, and_3_out, and_4_out, and_5_out, and_6_out, and_7_out, decoder_1_out0,
       decoder_1_out1, decoder_1_out2, decoder_1_out3, decoder_1_out4, decoder_1_out5, decoder_1_out6;
  wire [7:0] sp_q, t0_q, t1_q, t2_q, t3_q, t4_q, zero_q;

  Decoder #(.select(4), .enable("false")) decoder_1 (
    .out0(decoder_1_out0), .out1(decoder_1_out1), .out2(decoder_1_out2), .out3(decoder_1_out3),
    .out4(decoder_1_out4), .out5(decoder_1_out5), .out6(decoder_1_out6), .sel(Write_reg_4_bit));  // open: out7, out8, out9, out10, out11, out12, out13, out14, out15
  Register zero (.D(write_data_8_bit), .en(and_1_out), .Q(zero_q), .clk(Clock), .clr(reset));
  and and_1 (and_1_out, decoder_1_out0, RegWrite);
  Register sp (.D(write_data_8_bit), .en(and_2_out), .Q(sp_q), .clk(Clock), .clr(reset));
  and and_2 (and_2_out, decoder_1_out1, RegWrite);
  Register t0 (.D(write_data_8_bit), .en(and_3_out), .Q(t0_q), .clk(Clock), .clr(reset));
  and and_3 (and_3_out, decoder_1_out2, RegWrite);
  Register t1 (.D(write_data_8_bit), .en(and_4_out), .Q(t1_q), .clk(Clock), .clr(reset));
  and and_4 (and_4_out, decoder_1_out3, RegWrite);
  Register t2 (.D(write_data_8_bit), .en(and_5_out), .Q(t2_q), .clk(Clock), .clr(reset));
  and and_5 (and_5_out, decoder_1_out4, RegWrite);
  Register t3 (.D(write_data_8_bit), .en(and_6_out), .Q(t3_q), .clk(Clock), .clr(reset));
  and and_6 (and_6_out, decoder_1_out5, RegWrite);
  Register t4 (.D(write_data_8_bit), .en(and_7_out), .Q(t4_q), .clk(Clock), .clr(reset));
  and and_7 (and_7_out, decoder_1_out6, RegWrite);
  Multiplexer #(.select(4), .width(8), .enable("false")) multiplexer_1 (
    .in0(zero_q), .in1(sp_q), .in2(t0_q), .in3(t1_q), .in4(t2_q), .in5(t3_q), .in6(t4_q), .out(read_data_1),
    .sel(Read_reg1));  // open: in7, in8, in9, in10, in11, in12, in13, in14, in15
  Multiplexer #(.select(4), .width(8), .enable("false")) multiplexer_2 (
    .in0(zero_q), .in1(sp_q), .in2(t0_q), .in3(t1_q), .in4(t2_q), .in5(t3_q), .in6(t4_q), .out(read_data_2),
    .sel(Read_reg2));  // open: in7, in8, in9, in10, in11, in12, in13, in14, in15

  // Notes on the sheet:
  //   REGISTERs
  //   0-6
  //   0-6
endmodule

module Data___Stack_Memory (
  input  MemWrite,
  input  [7:0] Address,
  input  [7:0] WriteData,
  input  Clock,
  input  MemRead,
  input  isStack,
  input  reset,
  output [7:0] ReadData
);

  wire and_1_out, and_2_out, and_3_out, and_4_out, not_1_out, not_2_out;
  wire [7:0] ram_1_data, ram_2_data;

  and and_1 (and_1_out, MemWrite, isStack);
  and and_2 (and_2_out, MemWrite, not_1_out);
  not not_1 (not_1_out, isStack);
  and and_3 (and_3_out, MemRead, not_2_out);
  RAM #(.bus("separate")) ram_1 (
    .addr(Address), .din(WriteData), .data(ram_1_data), .str(and_1_out), .clk(Clock), .ld(and_4_out),
    .clr(reset));  // open: sel
  and and_4 (and_4_out, MemRead, isStack);
  RAM #(.bus("separate")) ram_2 (
    .addr(Address), .din(WriteData), .data(ram_2_data), .str(and_2_out), .clk(Clock), .ld(and_3_out),
    .clr(reset));  // open: sel
  not not_2 (not_2_out, isStack);
  Multiplexer #(.width(8), .enable("false")) multiplexer_1 (
    .in0(ram_2_data), .in1(ram_1_data), .out(ReadData), .sel(isStack));

  // Notes on the sheet:
  //   8-bit address, 8-bit data
  //   Stack Memory(RAM)
  //   8-bit address, 8-bit data
  //   Data Memory(RAM)
  //   DATA & STACK MEMORY
  //   memory selector
endmodule

module PC (
  input  [7:0] Next_Address,
  input  clock,
  input  reset,
  output [7:0] Current_Address
);

  Register Program_Counter (.D(Next_Address), .Q(Current_Address), .clk(clock), .clr(reset));  // open: en

  // Notes on the sheet:
  //   PROGRAM COUNTER
endmodule
